// Logisim project dgof.circ as structural Verilog: 1 circuit, main circuit main
module main (
  input  [7:0] in_1,
  input  [7:0] in_2,
  output out_3
);

  wire clock_1_out, clock_2_out, not_1_out, or_2_out, or_3_out, or_4_out, or_5_out, or_6_out, or_7_out,
       or_8_out, undriven;
  wire [7:0] acum_q, adder_1_out, and_1_out, multiplexer_1_out, multiplexer_2_out, or_1_out, PC_q,
       register_1_q, subtractor_1_out;
  wire [15:0] Control_data, IR_q, rom_1_data;

  Register PC (.clk(clock_1_out), .Q(PC_q));  // open: D, en, clr
  Clock clock_1 (.out(clock_1_out));
  ROM #(.dataWidth(16)) Control (.addr(rom_1_data[7:0]), .data(Control_data));
  ROM #(.dataWidth(16)) rom_1 (.addr(PC_q), .data(rom_1_data));
  Register #(.width(16)) IR (.D(rom_1_data), .clk(clock_2_out), .Q({IR_q[15:6], IR_q[6], IR_q[4:0]}));  // open: en, clr
  Clock clock_2 (.out(clock_2_out));
  Register acum (.D(multiplexer_1_out), .Q(acum_q));  // open: en, clk, clr
  Multiplexer #(.width(8)) multiplexer_1 (
    .in0({IR_q[7:6], IR_q[6], IR_q[4:0]}), .in1({IR_q[7:6], IR_q[6], IR_q[4:0]}), .out(multiplexer_1_out));  // open: sel
  Register register_1 (.D(IR_q[15:8]), .Q(register_1_q));  // open: en, clk, clr
  Multiplexer #(.width(8)) multiplexer_2 (
    .in1(register_1_q), .out(multiplexer_2_out), .sel(Control_data[0]));  // open: in0
  Adder adder_1 (.a(in_1), .b(in_1), .out(adder_1_out));  // open: cin, cout
  Subtractor subtractor_1 (.a(in_1), .b(in_1), .out(subtractor_1_out));  // open: bin, bout
  assign or_1_out = in_1 | in_1;  // OR_Gate or_1, 8 bits wide
  assign and_1_out = in_1 & in_1;  // AND_Gate and_1, 8 bits wide
  Multiplexer #(.select(2), .width(8)) multiplexer_3 (
    .in0(and_1_out), .in1(adder_1_out), .in2(subtractor_1_out), .in3(or_1_out),
    .out({IR_q[7:6], IR_q[6], IR_q[4:0]}), .sel(Control_data[2:1]));
  RAM ram_1 (
    .addr({IR_q[7:6], IR_q[6], IR_q[4:0]}), .we(Control_data[3]), .oe(rom_1_data[0]), .clk(rom_1_data[0]),
    .din(rom_1_data[7:0]));  // open: dout
  or or_2 (or_2_out, IR_q[0], IR_q[1]);
  or or_3 (or_3_out, IR_q[2], IR_q[3]);
  or or_4 (or_4_out, IR_q[4], IR_q[6]);
  or or_5 (or_5_out, IR_q[6], IR_q[7]);
  or or_6 (or_6_out, or_2_out, or_3_out);
  or or_7 (or_7_out, or_4_out, or_5_out);
  or or_8 (or_8_out, or_6_out, or_7_out);
  not not_1 (not_1_out, or_8_out);
  Register #(.width(1)) flag (.D(not_1_out), .en(undriven), .clk(undriven), .Q(out_3));  // open: clr
  // Pins of 8 and 16 bits meet at Control_data
  // Pins of 1 and 8 and 16 bits meet at rom_1_data

  assign in_2 = in_1;
endmodule
