// Logisim project ñkdfsm.circ as structural Verilog: 1 circuit, main circuit main
module main (
  input  [7:0] in_1,
  output out_2
);

  wire clock_1_out, clock_2_out, clock_3_out, not_1_out, or_2_out, or_3_out, or_4_out, or_5_out, or_6_out,
       or_7_out, or_8_out;
  wire [3:0] IR_q;
  wire [7:0] acu_q, adder_1_out, adder_2_out, and_1_out, multiplexer_1_out, multiplexer_2_out,
       multiplexer_3_out, nand_1_out, nor_1_out, or_1_out, PC_q, ram_1_dout, register_1_q, subtractor_1_out,
       xnor_1_out, xor_1_out;
  wire [7:4] IR_q_2;
  wire [15:0] Control_data, rom_1_data;

  Register PC (.D(multiplexer_2_out), .en(Control_data[4]), .clk(clock_1_out), .Q(PC_q));  // open: clr
  Clock clock_1 (.out(clock_1_out));
  ROM #(.dataWidth(16)) rom_1 (.addr(PC_q), .data(rom_1_data));
  Adder adder_1 (.a(PC_q), .b(in_1), .out(adder_1_out));  // open: cin, cout
  ROM #(.addrWidth(4), .dataWidth(16)) Control (.addr(IR_q_2), .data(Control_data));
  Clock clock_2 (.out(clock_2_out));
  Clock clock_3 (.out(clock_3_out));
  Register register_1 (.D(rom_1_data[7:0]), .en(Control_data[3]), .clk(clock_2_out), .Q(register_1_q));  // open: clr
  Register IR (.D(rom_1_data[15:8]), .en(Control_data[3]), .clk(clock_3_out), .Q({IR_q_2, IR_q}));  // open: clr
  Register acu (.D(multiplexer_1_out), .en(Control_data[6]), .Q(acu_q), .clr(Control_data[7]));  // open: clk
  Multiplexer #(.width(8)) multiplexer_1 (
    .in0({multiplexer_3_out[7:6], multiplexer_3_out[6], multiplexer_3_out[4:0]}), .in1(register_1_q),
    .out(multiplexer_1_out), .sel(Control_data[9]));
  Multiplexer #(.width(8)) multiplexer_2 (
    .in0(adder_1_out), .out(multiplexer_2_out), .sel(Control_data[10]));  // open: in1
  assign xnor_1_out = ~(acu_q ^ {IR_q_2, IR_q});  // XNOR_Gate xnor_1, 8 bits wide
  Adder adder_2 (.a(acu_q), .b({IR_q_2, IR_q}), .out(adder_2_out));  // open: cin, cout
  Subtractor subtractor_1 (.a(acu_q), .b({IR_q_2, IR_q}), .out(subtractor_1_out));  // open: bin, bout
  assign xor_1_out = acu_q ^ {IR_q_2, IR_q};  // XOR_Gate xor_1, 8 bits wide
  assign nand_1_out = ~(acu_q & {IR_q_2, IR_q});  // NAND_Gate nand_1, 8 bits wide
  assign and_1_out = acu_q & {IR_q_2, IR_q};  // AND_Gate and_1, 8 bits wide
  assign or_1_out = acu_q | {IR_q_2, IR_q};  // OR_Gate or_1, 8 bits wide
  assign nor_1_out = ~(acu_q | {IR_q_2, IR_q});  // NOR_Gate nor_1, 8 bits wide
  Multiplexer #(.select(3), .width(8)) multiplexer_3 (
    .in0(adder_2_out), .in1(subtractor_1_out), .in2(xor_1_out), .in3(nand_1_out), .in4(and_1_out),
    .in5(or_1_out), .in6(nor_1_out), .in7(xnor_1_out),
    .out({multiplexer_3_out[7:6], multiplexer_3_out[6], multiplexer_3_out[4:0]}), .sel(Control_data[2:0]));
  or or_2 (or_2_out, multiplexer_3_out[0], multiplexer_3_out[1]);
  or or_3 (or_3_out, multiplexer_3_out[2], multiplexer_3_out[3]);
  or or_4 (or_4_out, multiplexer_3_out[4], multiplexer_3_out[6]);
  or or_5 (or_5_out, multiplexer_3_out[6], multiplexer_3_out[7]);
  RAM ram_1 (
    .addr({multiplexer_3_out[7:6], multiplexer_3_out[6], multiplexer_3_out[4:0]}), .we(Control_data[8]),
    .oe(Control_data[7]), .din({IR_q_2, IR_q}), .dout(ram_1_dout));  // open: clk
  or or_6 (or_6_out, or_2_out, or_3_out);
  or or_7 (or_7_out, or_4_out, or_5_out);
  or or_8 (or_8_out, or_6_out, or_7_out);
  Multiplexer #(.width(8)) multiplexer_4 (
    .in0(ram_1_dout), .in1({multiplexer_3_out[7:6], multiplexer_3_out[6], multiplexer_3_out[4:0]}),
    .sel(Control_data[11]));  // open: out
  not not_1 (not_1_out, or_8_out);
  Register #(.width(1)) flag (.D(not_1_out), .en(Control_data[5]), .clk(Control_data[5]), .Q(out_2));  // open: clr
  Clock clock_4 (.out(Control_data[5]));
endmodule
